# Fritzing sketch Projeto1 (saved by Fritzing 0.8.7b)
breadboards: 1

parts:
  Componente1 = Arduino Uno (Rev3)
  LED1 = LED - 5mm [color="Red (633nm)" package="5 mm [THT]"]
  LED2 = smd LED [color="Green (570nm)" package="0805 [SMD]"]
  R1 = Rotary Potentiometer (Small) [maximum_resistance=100kΩ package=THT]
  S1 = Pushbutton [package="[THT]"]
  R2 = Resistor [package="0402 [SMD]"]
  R2_2 = Resistor [tolerance=±5% resistance=220 package=THT]

nets:
  N1: Componente1.A5/SCL, R1.wiper
  N2: Componente1.D8, LED1.cathode
  N3: Componente1.D13/SCK, LED2.cathode
  N4: Componente1.D4, S1.Pin_1, S1.Pin_2, R2.Pin_0, R2_2.Pin_0
  N5: Componente1.5V, R1.leg2, S1.Pin_3, S1.Pin_4
  N6: Componente1.GND, LED1.anode, LED2.anode, R1.leg1, R2.Pin_1, R2_2.Pin_1
